// Logisim project SomadorPRC4B_andreLuisQuiosi.circ as structural Verilog: 1 circuit, main circuit main
module main (
  input  Carry_Cin,
  input  [3:0] A,
  input  [3:0] B,
  output Cout,
  output [3:0] S
);

  wire and_1_out, and_2_out, and_3_out, and_4_out, and_5_out, and_6_out, and_7_out, and_8_out, Cout1_out,
       Cout2_out, Cout3_out, xor_1_out, xor_2_out, xor_3_out, xor_4_out;

  xor xor_1 (xor_1_out, A[0], B[0]);
  xor xor_2 (xor_2_out, A[1], B[1]);
  xor xor_3 (xor_3_out, A[2], B[2]);
  xor xor_4 (xor_4_out, A[3], B[3]);
  xor S1 (S[0], xor_1_out, Carry_Cin);
  and and_1 (and_1_out, Carry_Cin, xor_1_out);
  and and_2 (and_2_out, B[0], A[0]);
  xor S2 (S[1], xor_2_out, Cout1_out);
  and and_3 (and_3_out, Cout1_out, xor_2_out);
  and and_4 (and_4_out, B[1], A[1]);
  xor S3 (S[2], xor_3_out, Cout2_out);
  and and_5 (and_5_out, Cout2_out, xor_3_out);
  and and_6 (and_6_out, B[2], A[2]);
  xor S4 (S[3], xor_4_out, Cout3_out);
  and and_7 (and_7_out, Cout3_out, xor_4_out);
  and and_8 (and_8_out, B[3], A[3]);
  or Cout1 (Cout1_out, and_1_out, and_2_out);
  or Cout2 (Cout2_out, and_3_out, and_4_out);
  or Cout3 (Cout3_out, and_5_out, and_6_out);
  or Cout4 (Cout, and_7_out, and_8_out);
endmodule
